// Logisim project ALU Design 09_03_23.circ as structural Verilog
module Basic_ALU (
  input  [3:0] in_1,
  input  [3:0] in_2,
  input  [1:0] in_3,
  input  [1:0] in_4,
  output [3:0] out_5,
  output out_6
);

  wire [3:0] adder_1_out, and_1_out, shifter_1_out, subtractor_1_out;

  Adder #(.width(4)) adder_1 (.a(in_1), .b(in_2), .out(adder_1_out));  // open: cin, cout
  Subtractor #(.width(4)) subtractor_1 (.a(in_1), .b(in_2), .out(subtractor_1_out));  // open: bin, bout
  Shifter #(.width(4)) shifter_1 (.in(in_1), .\dist (in_3), .out(shifter_1_out));
  assign and_1_out = in_1 & in_2;  // AND_Gate and_1, 4 bits wide
  Multiplexer #(.select(2), .width(4), .enable("false")) multiplexer_1 (
    .in0(and_1_out), .in1(adder_1_out), .in2(subtractor_1_out), .in3(shifter_1_out), .out(out_5), .sel(in_4));
  nor nor_1 (out_6, out_5[0], out_5[1], out_5[2], out_5[3]);
endmodule
