// Logisim project Datapath_project.circ as structural Verilog: 8 circuits, main circuit Datapath
module _10_bt_registor (
  input  [9:0] IN,
  input  in_2,
  input  Enable,
  output [9:0] OUT
);

  D_Flip_Flop d_ff_1 (.clk(in_2), .D(IN[0]), .Q(OUT[0]), .en(Enable));  // open: Qn, preset, reset
  D_Flip_Flop d_ff_2 (.clk(in_2), .D(IN[2]), .Q(OUT[2]), .en(Enable));  // open: Qn, preset, reset
  D_Flip_Flop d_ff_3 (.clk(in_2), .D(IN[4]), .Q(OUT[4]), .en(Enable));  // open: Qn, preset, reset
  D_Flip_Flop d_ff_4 (.clk(in_2), .D(IN[6]), .Q(OUT[6]), .en(Enable));  // open: Qn, preset, reset
  D_Flip_Flop d_ff_5 (.clk(in_2), .D(IN[8]), .Q(OUT[8]), .en(Enable));  // open: Qn, preset, reset
  D_Flip_Flop d_ff_6 (.clk(in_2), .D(IN[1]), .Q(OUT[1]), .en(Enable));  // open: Qn, preset, reset
  D_Flip_Flop d_ff_7 (.clk(in_2), .D(IN[3]), .Q(OUT[3]), .en(Enable));  // open: Qn, preset, reset
  D_Flip_Flop d_ff_8 (.clk(in_2), .D(IN[5]), .Q(OUT[5]), .en(Enable));  // open: Qn, preset, reset
  D_Flip_Flop d_ff_9 (.clk(in_2), .D(IN[7]), .Q(OUT[7]), .en(Enable));  // open: Qn, preset, reset
  D_Flip_Flop d_ff_10 (.clk(in_2), .D(IN[9]), .Q(OUT[9]), .en(Enable));  // open: Qn, preset, reset
endmodule

module _10_bit_registor_file (
  input  [9:0] in_1,
  input  [2:0] Address,
  input  [2:0] in_3,
  input  Write,
  input  in_5,
  input  [2:0] in_6,
  output [9:0] out_7,
  output [9:0] T0,
  output [9:0] out_9
);

  wire decoder_1_out0, decoder_1_out1, decoder_1_out2, decoder_1_out3, decoder_1_out4, decoder_1_out5,
       decoder_1_out6, decoder_1_out7;
  wire [9:0] n10_bt_registor_1_out, n10_bt_registor_2_out, n10_bt_registor_3_out, n10_bt_registor_4_out,
       n10_bt_registor_5_out, n10_bt_registor_7_out, n10_bt_registor_8_out;

  Decoder #(.select(3), .disabled(0)) decoder_1 (
    .out0(decoder_1_out0), .out1(decoder_1_out1), .out2(decoder_1_out2), .out3(decoder_1_out3),
    .out4(decoder_1_out4), .out5(decoder_1_out5), .out6(decoder_1_out6), .out7(decoder_1_out7),
    .sel(Address), .en(Write));
  _10_bt_registor u_10_bt_registor_1 (
    .IN({10{1'b0}}), .Enable(decoder_1_out0), .OUT(n10_bt_registor_1_out), .in_2(in_5));
  _10_bt_registor u_10_bt_registor_2 (.IN(in_1), .Enable(decoder_1_out2), .OUT(n10_bt_registor_2_out), .in_2(in_5));
  _10_bt_registor u_10_bt_registor_3 (.IN(in_1), .Enable(decoder_1_out4), .OUT(n10_bt_registor_3_out), .in_2(in_5));
  _10_bt_registor u_10_bt_registor_4 (.IN(in_1), .Enable(decoder_1_out6), .OUT(n10_bt_registor_4_out), .in_2(in_5));
  _10_bt_registor u_10_bt_registor_5 (.IN(in_1), .Enable(decoder_1_out1), .OUT(n10_bt_registor_5_out), .in_2(in_5));
  _10_bt_registor u_10_bt_registor_6 (.IN(in_1), .Enable(decoder_1_out3), .OUT(T0), .in_2(in_5));
  _10_bt_registor u_10_bt_registor_7 (.IN(in_1), .Enable(decoder_1_out5), .OUT(n10_bt_registor_7_out), .in_2(in_5));
  _10_bt_registor u_10_bt_registor_8 (.IN(in_1), .Enable(decoder_1_out7), .OUT(n10_bt_registor_8_out), .in_2(in_5));
  Multiplexer #(.select(3), .width(10), .enable("false")) multiplexer_1 (
    .in0(n10_bt_registor_1_out), .in1(n10_bt_registor_5_out), .in2(n10_bt_registor_2_out), .in3(T0),
    .in4(n10_bt_registor_3_out), .in5(n10_bt_registor_7_out), .in6(n10_bt_registor_4_out),
    .in7(n10_bt_registor_8_out), .out(out_7), .sel(in_3));
  Multiplexer #(.select(3), .width(10), .enable("false")) multiplexer_2 (
    .in0(n10_bt_registor_1_out), .in1(n10_bt_registor_5_out), .in2(n10_bt_registor_2_out), .in3(T0),
    .in4(n10_bt_registor_3_out), .in5(n10_bt_registor_7_out), .in6(n10_bt_registor_4_out),
    .in7(n10_bt_registor_8_out), .out(out_9), .sel(in_6));
endmodule

module _10_bit_ALU (
  input  [2:0] in_1,
  input  [9:0] in_2,
  input  [9:0] in_3,
  input  in_4,
  output [9:0] out_5,
  output out_6,
  output out_7,
  output out_8
);

  wire n1bit_alu_1_cout, n1bit_alu_2_cout, n1bit_alu_3_cout, n1bit_alu_4_cout, n1bit_alu_5_cout,
       n1bit_alu_6_cout, n1bit_alu_7_cout, n1bit_alu_8_cout, n1bit_alu_9_cout, n1bit_alu_10_sltout;
  wire [3:0] bit_extender_1_out;
  wire [9:0] shifter_1_out, shifter_2_out;

  Bit_Extender #(.in_width(10), .out_width(4)) bit_extender_1 (.in(in_3), .out(bit_extender_1_out));
  Shifter #(.width(10)) shifter_1 (.in(in_2), .\dist (bit_extender_1_out), .out(shifter_1_out));
  Shifter #(.width(10), .shift("lr")) shifter_2 (.in(in_2), .\dist (bit_extender_1_out), .out(shifter_2_out));
  _1bit_ALU u_1bit_alu_1 (
    .A(in_2[0]), .B(in_3[0]), .Bin(in_4), .ALUop(in_1), .Result(out_5[0]), .Cout(n1bit_alu_1_cout),
    .srl(shifter_2_out[0]), .sll(shifter_1_out[0]), .slt(n1bit_alu_10_sltout), .Cin(in_4));  // open: sltout
  _1bit_ALU u_1bit_alu_2 (
    .A(in_2[1]), .B(in_3[1]), .Bin(in_4), .ALUop(in_1), .Result(out_5[1]), .Cout(n1bit_alu_2_cout),
    .srl(shifter_2_out[1]), .sll(shifter_1_out[1]), .slt(1'b0), .Cin(n1bit_alu_1_cout));  // open: sltout
  _1bit_ALU u_1bit_alu_3 (
    .A(in_2[2]), .B(in_3[2]), .Bin(in_4), .ALUop(in_1), .Result(out_5[2]), .Cout(n1bit_alu_3_cout),
    .srl(shifter_2_out[2]), .sll(shifter_1_out[2]), .slt(1'b0), .Cin(n1bit_alu_2_cout));  // open: sltout
  _1bit_ALU u_1bit_alu_4 (
    .A(in_2[3]), .B(in_3[3]), .Bin(in_4), .ALUop(in_1), .Result(out_5[3]), .Cout(n1bit_alu_4_cout),
    .srl(shifter_2_out[3]), .sll(shifter_1_out[3]), .slt(1'b0), .Cin(n1bit_alu_3_cout));  // open: sltout
  _1bit_ALU u_1bit_alu_5 (
    .A(in_2[4]), .B(in_3[4]), .Bin(in_4), .ALUop(in_1), .Result(out_5[4]), .Cout(n1bit_alu_5_cout),
    .srl(shifter_2_out[4]), .sll(shifter_1_out[4]), .slt(1'b0), .Cin(n1bit_alu_4_cout));  // open: sltout
  _1bit_ALU u_1bit_alu_6 (
    .A(in_2[5]), .B(in_3[5]), .Bin(in_4), .ALUop(in_1), .Result(out_5[5]), .Cout(n1bit_alu_6_cout),
    .srl(shifter_2_out[5]), .sll(shifter_1_out[5]), .slt(1'b0), .Cin(n1bit_alu_5_cout));  // open: sltout
  _1bit_ALU u_1bit_alu_7 (
    .A(in_2[6]), .B(in_3[6]), .Bin(in_4), .ALUop(in_1), .Result(out_5[6]), .Cout(n1bit_alu_7_cout),
    .srl(shifter_2_out[6]), .sll(shifter_1_out[6]), .slt(1'b0), .Cin(n1bit_alu_6_cout));  // open: sltout
  _1bit_ALU u_1bit_alu_8 (
    .A(in_2[7]), .B(in_3[7]), .Bin(in_4), .ALUop(in_1), .Result(out_5[7]), .Cout(n1bit_alu_8_cout),
    .srl(shifter_2_out[7]), .sll(shifter_1_out[7]), .slt(1'b0), .Cin(n1bit_alu_7_cout));  // open: sltout
  _1bit_ALU u_1bit_alu_9 (
    .A(in_2[8]), .B(in_3[8]), .Bin(in_4), .ALUop(in_1), .Result(out_5[8]), .Cout(n1bit_alu_9_cout),
    .srl(shifter_2_out[8]), .sll(shifter_1_out[8]), .slt(1'b0), .Cin(n1bit_alu_8_cout));  // open: sltout
  _1bit_ALU u_1bit_alu_10 (
    .A(in_2[9]), .B(in_3[9]), .Bin(in_4), .ALUop(in_1), .Result(out_5[9]), .Cout(out_8),
    .srl(shifter_2_out[9]), .sll(shifter_1_out[9]), .slt(1'b0), .sltout(n1bit_alu_10_sltout),
    .Cin(n1bit_alu_9_cout));
  nor nor_1 (out_6, out_5[0], out_5[1], out_5[2], out_5[3], out_5[4], out_5[6], out_5[7], out_5[8], out_5[9]);
  xor xor_1 (out_7, n1bit_alu_9_cout, out_8);
endmodule

// Opcode
module _1bit_ALU (
  input  Cin,
  input  A,
  input  B,
  input  Bin,
  input  srl,
  input  sll,
  input  slt,
  input  [2:0] ALUop,
  output Result,
  output sltout,
  output Cout
);

  wire multiplexer_1_out, nand_1_out, nor_1_out, not_1_out;

  not not_1 (not_1_out, B);
  Multiplexer #(.disabled(0), .enable("false")) multiplexer_1 (
    .in0(B), .in1(not_1_out), .out(multiplexer_1_out), .sel(Bin));
  nand nand_1 (nand_1_out, A, B);
  nor nor_1 (nor_1_out, A, B);
  Adder #(.width(1)) adder_1 (.a(A), .b(multiplexer_1_out), .out(sltout), .cin(Cin), .cout(Cout));
  Multiplexer #(.select(3), .disabled(0), .enable("false")) multiplexer_2 (
    .in0(nand_1_out), .in1(nor_1_out), .in2(sltout), .in3(srl), .in4(sll), .in5(slt), .out(Result),
    .sel(ALUop));  // open: in6, in7
endmodule

module CU (
  input  op3,
  input  op2,
  input  op1,
  input  op0,
  output alu_op2,
  output alu_op1,
  output alu_op0,
  output bin,
  output alu_src,
  output r_write,
  output mem_to_reg,
  output mem_read,
  output mem_write,
  output branch,
  output jump,
  output in,
  output out
);

  wire and_1_out, and_2_out, and_3_out, and_4_out, and_5_out, and_6_out, and_7_out, and_8_out, and_9_out,
       and_10_out, and_11_out, and_12_out, and_13_out, and_14_out, and_15_out, not_1_out, not_2_out,
       not_3_out, not_4_out, not_5_out, not_6_out, not_7_out, not_8_out, not_9_out, not_10_out, not_11_out,
       not_12_out, not_13_out, not_14_out, not_15_out, not_16_out, not_17_out, not_18_out, not_19_out,
       not_20_out, not_21_out, not_22_out, not_23_out, not_24_out, not_25_out, not_26_out, not_27_out;

  and and_1 (and_1_out, op2, not_1_out, not_2_out);
  not not_1 (not_1_out, op1);
  not not_2 (not_2_out, op0);
  and and_2 (and_2_out, op3, op1, op0);
  not not_3 (not_3_out, op3);
  and and_3 (and_3_out, not_3_out, not_4_out);
  not not_4 (not_4_out, op2);
  not not_5 (not_5_out, op2);
  and and_4 (and_4_out, not_5_out, not_6_out);
  not not_6 (not_6_out, op0);
  not not_7 (not_7_out, op1);
  and and_5 (and_5_out, not_7_out, op0);
  and and_6 (and_6_out, op2, op0);
  and and_7 (and_7_out, op3, op1, op0);
  and and_8 (and_8_out, op3, op2);
  not not_8 (not_8_out, op3);
  and and_9 (and_9_out, not_8_out, op0);
  and and_10 (and_10_out, op3, op1);
  not not_9 (not_9_out, op3);
  not not_10 (not_10_out, op2);
  and and_11 (and_11_out, not_9_out, not_10_out, op1);
  and and_12 (and_12_out, op3, not_11_out);
  not not_11 (not_11_out, op1);
  not not_12 (not_12_out, op3);
  not not_13 (not_13_out, op1);
  and and_13 (and_13_out, not_13_out, not_14_out);
  not not_14 (not_14_out, op0);
  not not_15 (not_15_out, op2);
  and and_14 (and_14_out, not_15_out, op1, op0);
  and and_15 (and_15_out, op2, not_16_out);
  not not_16 (not_16_out, op0);
  not not_17 (not_17_out, op2);
  and and_16 (mem_to_reg, op3, not_17_out, not_18_out);
  not not_18 (not_18_out, op1);
  not not_19 (not_19_out, op2);
  not not_20 (not_20_out, op1);
  not not_21 (not_21_out, op0);
  not not_22 (not_22_out, op2);
  not not_23 (not_23_out, op1);
  not not_24 (not_24_out, op2);
  not not_25 (not_25_out, op0);
  not not_26 (not_26_out, op1);
  not not_27 (not_27_out, op0);
  or or_1 (alu_op2, and_1_out, and_2_out);
  or or_2 (alu_op1, and_3_out, and_4_out, and_5_out);
  or or_3 (alu_op0, and_6_out, and_7_out, and_8_out);
  or or_4 (bin, and_9_out, op2, and_10_out);
  or or_5 (alu_src, and_11_out, and_12_out);
  or or_6 (r_write, not_12_out, and_13_out, and_14_out, and_15_out);
  and and_17 (mem_read, op3, not_19_out, not_20_out, not_21_out);
  and and_18 (mem_write, op3, not_22_out, not_23_out, op0);
  and and_19 (branch, op3, not_24_out, op1, not_25_out);
  and and_20 (jump, op3, op2, not_26_out, op0);
  and and_21 (in, op3, op2, op1, not_27_out);
  and and_22 (out, op3, op2, op1, op0);
endmodule

module Datapath (
  input  in_1
);

  wire _0_out, _1_out, _2_out, _3_out, _4_out, _5_out, _6_out, _7_out, _8_out, _9_out, and_1_out, button_out,
       clock_1_out, clr_out, cu_1_alu_src, cu_1_bin, cu_1_branch, cu_1_jump, cu_1_mem_read, cu_1_mem_to_reg,
       cu_1_mem_write, cu_1_r_write, n10_bit_alu_1_out_6;
  wire [2:0] cu_1_alu_op0;
  wire [3:0] keyboard_1_out_13, keyboard_1_out_14, keyboard_1_out_15, keyboard_1_out_16, multiplexer_6_out,
       multiplexer_7_out, multiplexer_9_out, multiplexer_10_out, undriven_2, undriven_3, undriven_4,
       undriven_5;
  wire [9:0] adder_1_out, adder_2_out, adder_3_out, bit_extender_1_out, bit_extender_2_out,
       multiplexer_1_out, multiplexer_2_out, multiplexer_3_out, multiplexer_4_out, multiplexer_5_out,
       multiplexer_8_out, n10_bit_alu_1_out_5, n10_bit_registor_file_1_out_7, n10_bit_registor_file_1_out_9,
       n10_bit_registor_file_1_t0, ram_1_data, register_1_q, rom_1_data, undriven;

  Multiplexer #(.width(10), .enable("false")) multiplexer_1 (
    .in0(multiplexer_4_out), .in1(adder_2_out), .out(multiplexer_1_out), .sel(cu_1_jump));
  Register #(.width(10)) register_1 (.D(multiplexer_1_out), .Q(register_1_q), .clk(clock_1_out));  // open: en, clr
  Clock clock_1 (.out(clock_1_out));
  Adder #(.width(10)) adder_1 (.a(10'h1), .b(register_1_q), .out(adder_1_out));  // open: cin, cout
  Adder #(.width(10)) adder_2 (.a(adder_1_out), .b(bit_extender_1_out), .out(adder_2_out));  // open: cin, cout
  ROM #(.addrWidth(10), .dataWidth(10)) rom_1 (.addr(register_1_q), .data(rom_1_data));  // open: sel
  assign bit_extender_1_out = {{4{rom_1_data[5]}}, rom_1_data[5:0]};  // Bit_Extender bit_extender_1
  CU cu_1 (
    .op3(rom_1_data[9]), .alu_op2(cu_1_alu_op0[2]), .op2(rom_1_data[8]), .op1(rom_1_data[7]),
    .op0(rom_1_data[6]), .alu_op1(cu_1_alu_op0[1]), .alu_op0(cu_1_alu_op0[0]), .bin(cu_1_bin),
    .alu_src(cu_1_alu_src), .r_write(cu_1_r_write), .mem_to_reg(cu_1_mem_to_reg), .mem_read(cu_1_mem_read),
    .mem_write(cu_1_mem_write), .branch(cu_1_branch), .jump(cu_1_jump));  // open: in, out
  _10_bit_registor_file u_10_bit_registor_file_1 (
    .in_1(multiplexer_8_out), .in_3(rom_1_data[5:3]), .Address(rom_1_data[5:3]), .Write(cu_1_r_write),
    .in_6(rom_1_data[2:0]), .in_5(clock_1_out), .out_7(n10_bit_registor_file_1_out_7),
    .out_9(n10_bit_registor_file_1_out_9), .T0(n10_bit_registor_file_1_t0));
  assign bit_extender_2_out = {{7{1'b0}}, rom_1_data[2:0]};  // Bit_Extender bit_extender_2
  Button _1 (.out(_1_out));
  Button _2 (.out(_2_out));
  Button _4 (.out(_4_out));
  Button _5 (.out(_5_out));
  Button _7 (.out(_7_out));
  Button _8 (.out(_8_out));
  Button _0 (.out(_0_out));
  Button clr (.out(clr_out));
  Multiplexer #(.width(10), .enable("false")) multiplexer_2 (
    .in0(n10_bit_registor_file_1_out_7), .in1(n10_bit_registor_file_1_t0), .out(multiplexer_2_out),
    .sel(cu_1_branch));
  Multiplexer #(.width(10), .enable("false")) multiplexer_3 (
    .in0(n10_bit_registor_file_1_out_9), .in1(bit_extender_2_out), .out(multiplexer_3_out), .sel(cu_1_alu_src));
  Button _3 (.out(_3_out));
  keyboard keyboard_1 (
    .in_1(_1_out), .in_2(_2_out), .in_3(_3_out), .in_4(_4_out), .in_5(_5_out), .in_6(_6_out), .in_7(_7_out),
    .in_8(_8_out), .in_9(_9_out), .in_10(clr_out), .in_11(_0_out), .in_12(button_out),
    .out_13(keyboard_1_out_13), .out_14(keyboard_1_out_14), .out_15(keyboard_1_out_15),
    .out_16(keyboard_1_out_16));
  Button _6 (.out(_6_out));
  Button _9 (.out(_9_out));
  Button button (.out(button_out));
  _10_bit_ALU u_10_bit_alu_1 (
    .in_2(multiplexer_2_out), .in_3(multiplexer_3_out), .in_1(cu_1_alu_op0), .in_4(cu_1_bin),
    .out_5(n10_bit_alu_1_out_5), .out_6(n10_bit_alu_1_out_6));  // open: out_8, out_7
  Adder #(.width(10)) adder_3 (.a(adder_1_out), .b(bit_extender_2_out), .out(adder_3_out));  // open: cin, cout
  Multiplexer #(.width(10), .enable("false")) multiplexer_4 (
    .in0(adder_1_out), .in1(adder_3_out), .out(multiplexer_4_out), .sel(and_1_out));
  and and_1 (and_1_out, cu_1_branch, n10_bit_alu_1_out_6);
  Multiplexer #(.width(10), .enable("false")) multiplexer_5 (
    .in0(n10_bit_alu_1_out_5), .in1(ram_1_data), .out(multiplexer_5_out), .sel(cu_1_mem_to_reg));
  RAM #(.addrWidth(10), .dataWidth(10), .bus("separate")) ram_1 (
    .addr(n10_bit_alu_1_out_5), .din(n10_bit_registor_file_1_out_9), .data(ram_1_data), .str(cu_1_mem_write),
    .clk(clock_1_out), .ld(cu_1_mem_read));  // open: sel, clr
  Hex_Digit_Display hex_digit_display_1 (.value(multiplexer_6_out));  // open: dp
  Hex_Digit_Display hex_digit_display_2 (.value(multiplexer_7_out));  // open: dp
  Hex_Digit_Display hex_digit_display_3 (.value(multiplexer_9_out));  // open: dp
  Multiplexer #(.width(4), .disabled(0), .enable("false")) multiplexer_6 (
    .in0(undriven_5), .in1(keyboard_1_out_13), .out(multiplexer_6_out), .sel(in_1));
  Multiplexer #(.width(4), .disabled(0), .enable("false")) multiplexer_7 (
    .in0(undriven_4), .in1(keyboard_1_out_14), .out(multiplexer_7_out), .sel(in_1));
  Multiplexer #(.width(10), .enable("false")) multiplexer_8 (
    .in0(multiplexer_5_out), .in1(undriven), .out(multiplexer_8_out), .sel(in_1));
  Hex_Digit_Display hex_digit_display_4 (.value(multiplexer_10_out));  // open: dp
  Multiplexer #(.width(4), .disabled(0), .enable("false")) multiplexer_9 (
    .in0(undriven_3), .in1(keyboard_1_out_15), .out(multiplexer_9_out), .sel(in_1));
  Multiplexer #(.width(4), .disabled(0), .enable("false")) multiplexer_10 (
    .in0(undriven_2), .in1(keyboard_1_out_16), .out(multiplexer_10_out), .sel(in_1));

  // Notes on the sheet:
  //   contents of rom_1 (hex, n*v repeats v):
  //   49 8a a
  //   Control Unit
endmodule

module Test (
  input  [2:0] in_1,
  input  in_2,
  input  [9:0] in_3,
  input  [9:0] in_4,
  output [9:0] out_5
);

  wire n10_bit_alu_1_out_7;

  _10_bit_ALU u_10_bit_alu_1 (
    .in_2(in_3), .in_3(in_4), .in_1(in_1), .in_4(in_2), .out_5(out_5), .out_7(n10_bit_alu_1_out_7));  // open: out_8, out_6
endmodule

module keyboard (
  input  in_1,
  input  in_2,
  input  in_3,
  input  in_4,
  input  in_5,
  input  in_6,
  input  in_7,
  input  in_8,
  input  in_9,
  input  in_10,
  input  in_11,
  input  in_12,
  output [3:0] out_13,
  output [3:0] out_14,
  output [3:0] out_15,
  output [3:0] out_16
);

  wire or_1_out, priority_encoder_1_gs;
  wire [3:0] multiplexer_1_out, multiplexer_2_out, multiplexer_3_out, multiplexer_4_out,
       priority_encoder_1_out;

  Priority_Encoder #(.select(4)) priority_encoder_1 (
    .in0(in_11), .in1(in_1), .in2(in_2), .in3(in_3), .in4(in_4), .in5(in_5), .in6(in_6), .in7(in_7),
    .in8(in_8), .in9(in_9), .out(priority_encoder_1_out), .gs(priority_encoder_1_gs), .en_in(1'b1));  // open: in10, in11, in12, in13, in14, in15, en_out
  or or_1 (or_1_out, priority_encoder_1_gs, in_12);
  Multiplexer #(.width(4), .disabled(0), .enable("false")) multiplexer_1 (
    .in0(out_14), .in1(4'b0000), .out(multiplexer_1_out), .sel(in_12));
  Register #(.width(4), .trigger("falling")) register_1 (
    .D(multiplexer_1_out), .Q(out_13), .clk(or_1_out), .clr(in_10));  // open: en
  Multiplexer #(.width(4), .disabled(0), .enable("false")) multiplexer_2 (
    .in0(out_15), .in1(out_13), .out(multiplexer_2_out), .sel(in_12));
  Register #(.width(4), .trigger("falling")) register_2 (
    .D(multiplexer_2_out), .Q(out_14), .clk(or_1_out), .clr(in_10));  // open: en
  Multiplexer #(.width(4), .disabled(0), .enable("false")) multiplexer_3 (
    .in0(out_16), .in1(out_14), .out(multiplexer_3_out), .sel(in_12));
  Register #(.width(4), .trigger("falling")) register_3 (
    .D(multiplexer_3_out), .Q(out_15), .clk(or_1_out), .clr(in_10));  // open: en
  Multiplexer #(.width(4), .disabled(0), .enable("false")) multiplexer_4 (
    .in0(priority_encoder_1_out), .in1(out_15), .out(multiplexer_4_out), .sel(in_12));
  Register #(.width(4), .trigger("falling")) register_4 (
    .D(multiplexer_4_out), .Q(out_16), .clk(or_1_out), .clr(in_10));  // open: en
endmodule
