// Logisim project MIPS.circ as structural Verilog: 1 circuit, main circuit main
module main (
  input  Branch,
  input  in_2,
  input  Branch_2,
  input  MemWrite,
  input  in_5,
  input  MemToReg,
  input  MemRead,
  input  in_8,
  input  [1:0] Shamt,
  output [1:0] OppCode,
  output [3:0] Next_Addres,
  output [2:0] RS,
  output [2:0] RT,
  output [3:0] Read_1,
  output [3:0] Read_2,
  output [2:0] RD,
  output [3:0] Result
);

  wire and_1_out, basic_alu_1_p3, basic_alu_1_p7, Clk_out;
  wire [2:0] multiplexer_3_out;
  wire [3:0] adder_1_out, bit_extender_1_out, bit_extender_2_out, bit_extender_3_out, multiplexer_1_out,
       multiplexer_2_out, multiplexer_4_out, multiplexer_5_out, ram_2_data, register_1_q;

  and and_1 (and_1_out, basic_alu_1_p7, Branch);
  assign bit_extender_1_out = {{1{1'b0}}, RD};  // Bit_Extender bit_extender_1
  Adder #(.width(4)) adder_1 (.a(bit_extender_1_out), .b(Next_Addres), .out(adder_1_out));  // open: cin, cout
  Multiplexer #(.width(4), .disabled(0), .enable("false")) multiplexer_1 (
    .in0(Next_Addres), .in1(adder_1_out), .out(multiplexer_1_out), .sel(and_1_out));
  Register #(.width(4)) register_1 (.D(multiplexer_2_out), .Q(register_1_q), .clk(Clk_out));  // open: en, clr
  Multiplexer #(.width(4), .disabled(0), .enable("false")) multiplexer_2 (
    .in0(multiplexer_1_out), .in1(bit_extender_2_out), .out(multiplexer_2_out), .sel(Branch_2));
  Bit_Extender #(.in_width(9), .out_width(4)) bit_extender_2 (.in({RS, RT, RD}), .out(bit_extender_2_out));
  Clock Clk (.out(Clk_out));
  Adder #(.width(4)) adder_2 (.a(4'b0001), .b(register_1_q), .out(Next_Addres));  // open: cin, cout
  RAM #(.addrWidth(4), .dataWidth(11)) ram_1 (
    .addr(register_1_q), .data({OppCode, RS, RT, RD}), .clk(Clk_out));  // open: sel, ld, clr
  Multiplexer #(.width(3), .disabled(0), .enable("false")) multiplexer_3 (
    .in0(RD), .in1(RT), .out(multiplexer_3_out), .sel(in_2));
  Multiplexer #(.width(4), .disabled(0), .enable("false")) multiplexer_4 (
    .in0(Result), .in1(ram_2_data), .out(multiplexer_4_out), .sel(MemToReg));
  Register_File register_file_1 (
    .Read_Address_1(RS), .Read_Address_2(RT), .Data_1(Read_1), .Data_2(Read_2), .Data(multiplexer_4_out),
    .Clk(Clk_out), .Write_register_Address(multiplexer_3_out), .Write(in_8));
  assign bit_extender_3_out = {{1{1'b0}}, RD};  // Bit_Extender bit_extender_3
  Multiplexer #(.width(4), .disabled(0), .enable("false")) multiplexer_5 (
    .in0(Read_2), .in1(bit_extender_3_out), .out(multiplexer_5_out), .sel(in_5));
  // Basic_ALU basic_alu_1: pin names not known; wires that end beside it: Read_1, multiplexer_5_out, basic_alu_1_p3, basic_alu_1_p3, Shamt, OppCode, basic_alu_1_p7, Result
  RAM #(.addrWidth(4), .dataWidth(4), .bus("separate")) ram_2 (
    .addr(Result), .din(Read_2), .data(ram_2_data), .str(MemWrite), .clk(Clk_out), .ld(MemRead));  // open: sel, clr
endmodule
