// Logisim project Register File Design 02_03_23.circ as structural Verilog: 3 circuits, main circuit main
module main (
  input  [2:0] in_1,
  input  [2:0] in_2,
  input  [3:0] in_3,
  input  [2:0] in_4,
  input  in_5,
  output [3:0] out_6,
  output [3:0] out_7
);

  wire clock_1_out;

  Clock clock_1 (.out(clock_1_out));
  // Register_File register_file_1: pin names not known; wires that end beside it: in_1, in_3, in_2, in_4, in_5, clock_1_out, out_6, out_7
endmodule

module _4_bit_register (
  input  [3:0] Data,
  input  CLK,
  input  Enable,
  output [3:0] Output
);

  D_Flip_Flop d_ff_1 (.clk(CLK), .D(Data[0]), .Q(Output[0]), .en(Enable));  // open: Qn, preset, reset
  D_Flip_Flop d_ff_2 (.clk(CLK), .D(Data[1]), .Q(Output[1]), .en(Enable));  // open: Qn, preset, reset
  D_Flip_Flop d_ff_3 (.clk(CLK), .D(Data[2]), .Q(Output[2]), .en(Enable));  // open: Qn, preset, reset
  D_Flip_Flop d_ff_4 (.clk(CLK), .D(Data[3]), .Q(Output[3]), .en(Enable));  // open: Qn, preset, reset
endmodule

module Register_File (
  input  [3:0] Data,
  input  Write,
  input  [2:0] Write_register_Address,
  input  Clk,
  input  [2:0] Read_Address_1,
  input  [2:0] Read_Address_2,
  output [3:0] Data_1,
  output [3:0] Data_2
);

  wire decoder_1_out0, decoder_1_out1, decoder_1_out2, decoder_1_out3, decoder_1_out4;
  wire [3:0] n4_bit_register_1_output, n4_bit_register_2_output, n4_bit_register_3_output,
       n4_bit_register_4_output, n4_bit_register_5_output;

  Decoder #(.select(3), .disabled(0)) decoder_1 (
    .out0(decoder_1_out0), .out1(decoder_1_out1), .out2(decoder_1_out2), .out3(decoder_1_out3),
    .out4(decoder_1_out4), .sel(Write_register_Address), .en(Write));  // open: out5, out6, out7
  _4_bit_register u_4_bit_register_1 (
    .Data(Data), .Enable(decoder_1_out0), .Output(n4_bit_register_1_output), .CLK(Clk));
  _4_bit_register u_4_bit_register_2 (
    .Data(Data), .Enable(decoder_1_out1), .Output(n4_bit_register_2_output), .CLK(Clk));
  _4_bit_register u_4_bit_register_3 (
    .Data(Data), .Enable(decoder_1_out2), .Output(n4_bit_register_3_output), .CLK(Clk));
  _4_bit_register u_4_bit_register_4 (
    .Data(Data), .Enable(decoder_1_out3), .Output(n4_bit_register_4_output), .CLK(Clk));
  _4_bit_register u_4_bit_register_5 (
    .Data(Data), .Enable(decoder_1_out4), .Output(n4_bit_register_5_output), .CLK(Clk));
  Multiplexer #(.select(3), .width(4), .disabled(0), .enable("false")) multiplexer_1 (
    .in0(n4_bit_register_1_output), .in1(n4_bit_register_2_output), .in2(n4_bit_register_3_output),
    .in3(n4_bit_register_4_output), .in4(n4_bit_register_5_output), .out(Data_1), .sel(Read_Address_1));  // open: in5, in6, in7
  Multiplexer #(.select(3), .width(4), .disabled(0), .enable("false")) multiplexer_2 (
    .in0(n4_bit_register_1_output), .in1(n4_bit_register_2_output), .in2(n4_bit_register_3_output),
    .in3(n4_bit_register_4_output), .in4(n4_bit_register_5_output), .out(Data_2), .sel(Read_Address_2));  // open: in5, in6, in7
endmodule
